# Fritzing sketch schema-prototype-1.0 (saved by Fritzing 0.9.9b)

parts:
  MH-ET_LIVE_ESP32_DEVKIT1 = MH-ET LIVE ESP32 DEVKIT 38 pins
  Composant1 = LED Matrix - Serial Interface - Red/Green/Blue
  J1 = JST-03JQ-BT [part_number=JST-JQ-BT package=THT]
  J2 = Power Jack [package=power_jack_combo]
  Composant2 = INMP441

nets:
  3V3: MH-ET_LIVE_ESP32_DEVKIT1.3V3, Composant2.VDD
  N1: MH-ET_LIVE_ESP32_DEVKIT1.IO32, Composant2.SD
  N2: MH-ET_LIVE_ESP32_DEVKIT1.IO27, Composant1.MISO, J1.pin2
  N3: MH-ET_LIVE_ESP32_DEVKIT1.IO14, Composant2.SCK
  GND: MH-ET_LIVE_ESP32_DEVKIT1.GND#58, Composant1.GND, J1.pin1, J2.GND
  N4: MH-ET_LIVE_ESP32_DEVKIT1.5V, Composant1.CS, J1.pin3, J2.GNDBREAK
  N5: MH-ET_LIVE_ESP32_DEVKIT1.GND#64, Composant2.GND
  N6: MH-ET_LIVE_ESP32_DEVKIT1.GND#70, Composant2.L/R
  N7: MH-ET_LIVE_ESP32_DEVKIT1.IO15, Composant2.WS

notes:
  DC 5V - 16 AMP
  DIN
  DOUT

custom parts:
  MH-ET LIVE ESP32 DEVKIT 38 pins: http://mh.nodebb.com/topic/2/mh-et-live-esp32-devkit
  INMP441: This is a simple breakout board for the INMP441 I2S MEMS microphone.
